# Fritzing sketch 16x (saved by Fritzing 0.9.3b)

parts:
  Part2 = 16-Channel 12-bit PWM Servo Driver - I2C [part_number=815]
  Part3 = Arduino Nano (Rev3.0)
  JACK2 = 2.1mm Barrel Jack with Terminal Block
  C2 = Electrolytic Capacitor [capacitance=1000µF package="300 mil [THT, electrolytic]"]
  U1 = V_REG_LD1117VXX [package=78xxl]
  LED1 = LED - 5mm [color="Red (633nm)" package="5 mm [THT]"]
  LED2 = LED - 5mm [color="Red (633nm)" package="5 mm [THT]"]  # not connected
  LED3 = LED - 5mm [color="Red (633nm)" package="5 mm [THT]"]  # not connected
  LED4 = LED - 5mm [color="Red (633nm)" package="5 mm [THT]"]  # not connected
  LED5 = LED - 5mm [color="Red (633nm)" package="5 mm [THT]"]  # not connected
  LED6 = LED - 5mm [color="Red (633nm)" package="5 mm [THT]"]  # not connected
  LED7 = LED - 5mm [color="Red (633nm)" package="5 mm [THT]"]
  LED8 = LED - 5mm [color="Red (633nm)" package="5 mm [THT]"]  # not connected
  LED9 = LED - 5mm [color="Red (633nm)" package="5 mm [THT]"]
  LED10 = LED - 5mm [color="Red (633nm)" package="5 mm [THT]"]  # not connected
  LED11 = LED - 5mm [color="Red (633nm)" package="5 mm [THT]"]  # not connected
  LED12 = LED - 5mm [color="Red (633nm)" package="5 mm [THT]"]  # not connected
  LED13 = LED - 5mm [color="Red (633nm)" package="5 mm [THT]"]  # not connected
  LED14 = LED - 5mm [color="Red (633nm)" package="5 mm [THT]"]  # not connected
  LED15 = LED - 5mm [color="Red (633nm)" package="5 mm [THT]"]  # not connected
  LED16 = LED - 5mm [color="Red (633nm)" package="5 mm [THT]"]  # not connected
  J1 = Basic Servo

nets:
  N1: Part2.5.0V, C2.+, J1.vcc
  GND: Part2.GND, Part3.GND, JACK2.NEG, C2.-, J1.gnd
  N2: Part2.PWRIN, JACK2.POS
  N3: Part2.PWM7, J1.pulse
  VCC: Part2.VCC, Part3.5V
  N4: Part2.SDA, Part3.A4
  N5: Part2.SCL, Part3.A5
  N6: U1.IN, LED1.cathode
  N7: LED7.anode, LED9.cathode

custom parts:
  16-Channel 12-bit PWM Servo Driver - I2C: You want to make a cool robot, maybe a hexapod walker, or maybe just a piece of art with a lot of moving parts. Or maybe you want to drive a lot of LEDs with precise PWM output. Using only two pins, control 16 free-running PWM outputs! You can even chain up 62 breakouts to control up to 992 PWM outputs.
